# Fritzing sketch Untitled Sketch 2 (saved by Fritzing 0.9.3b)
circuit board: 4.61919cm x 5.70425cm
breadboards: 1

parts:
  U2 = ESP32S-HiLetgo [part_number=ESP32S-HiLetgo]
  IC1 = Voltage Regulator [package=to-220-alt]
  R1 = Resistor [tolerance=±5% resistance=220 package=THT]
  D2 = Schottky Diode [part_number=1N5817 package="300 mil [THT]"]
  U1 = L298 [package=multiwatt15]
  D1 = Schottky Diode [part_number=1N5817 package="300 mil [THT]"]
  M1 = DC Motor
  D3 = Schottky Diode [part_number=1N5817 package="300 mil [THT]"]
  J1_12V = Screw terminal - 2 pins [package=THT]
  D4 = Schottky Diode [part_number=1N5817 package="300 mil [THT]"]
  C1 = Ceramic Capacitor [capacitance=0.1µF package="0603 [SMD, multilayer]"]
  0_33uF = Ceramic Capacitor [capacitance="100 nF" package="0805 [SMD, multilayer]"]
  U4 = 74HC595 [package="DIP16 [THT]"]  # not connected

nets:
  N1: U2.VIN, IC1.OUT, U1.VLS, C1.1
  N2: IC1.GND, J1_12V.pin1, C1.0, 0_33uF.0
  N3: IC1.IN, J1_12V.pin2, 0_33uF.1
  N4: R1.Pin_0, D2.anode, U1.GND, D4.anode
  N5: R1.Pin_1, U1.CSA, U1.CSB
  N6: D2.cathode, U1.OUT2, U1.OUT3, D1.anode, M1.pin_2
  N7: U1.OUT1, U1.OUT4, M1.pin_1, D3.anode, D4.cathode
  N8: U1.VS, D1.cathode, D3.cathode
  N9: U1.IN1, U1.IN4
  N10: U1.ENA, U1.ENB
  N11: U1.IN2, U1.IN3

custom parts:
  ESP32S-HiLetgo: HiLetgo ESP-WROOM-32 ESP32 ESP-32S Development Board 2.4GHz Dual-Mode WiFi + Bluetooth Dual Cores Microcontroller The ESP32 integrated with Antenna switches, RF Balun, power amplifiers, low-noise amplifiers, filters, and management modules, and the entire solution occupies the least area of PCB. 2.4 GHz Wi-Fi plus Bluetooth dual-mode chip, with TSMC Ultra-low power consumption 40nm technology,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
